// Logisim project NSU-2023-T05L3e02.circ as structural Verilog: 3 circuits, main circuit cmp
module cmp (
  input  [7:0] A,
  input  [7:0] B,
  output Eq,
  output Gt
);

  wire and_1_out, and_2_out, and_3_out, and_4_out, and_5_out, and_6_out, and_7_out, comp_1_out_3,
       comp_1_out_4, comp_2_out_3, comp_2_out_4, comp_3_out_3, comp_3_out_4, comp_4_out_3, comp_4_out_4,
       comp_5_out_3, comp_5_out_4, comp_6_out_3, comp_6_out_4, comp_7_out_3, comp_7_out_4, comp_8_out_4,
       xnor_1_out, xnor_2_out, xnor_3_out, xnor_4_out, xnor_5_out, xnor_6_out, xnor_7_out, xnor_8_out;

  comp comp_1 (.in_1(A[7]), .in_2(B[7]), .out_3(comp_1_out_3), .out_4(comp_1_out_4));
  comp comp_2 (.in_1(A[6]), .in_2(B[6]), .out_3(comp_2_out_3), .out_4(comp_2_out_4));
  comp comp_3 (.in_1(A[4]), .in_2(B[4]), .out_3(comp_3_out_3), .out_4(comp_3_out_4));
  comp comp_4 (.in_1(A[5]), .in_2(B[5]), .out_3(comp_4_out_3), .out_4(comp_4_out_4));
  comp comp_5 (.in_1(A[3]), .in_2(B[3]), .out_3(comp_5_out_3), .out_4(comp_5_out_4));
  xnor xnor_1 (xnor_1_out, A[0], B[0]);
  xnor xnor_2 (xnor_2_out, A[1], B[1]);
  xnor xnor_3 (xnor_3_out, A[2], B[2]);
  xnor xnor_4 (xnor_4_out, A[3], B[3]);
  xnor xnor_5 (xnor_5_out, A[4], B[4]);
  xnor xnor_6 (xnor_6_out, A[5], B[5]);
  xnor xnor_7 (xnor_7_out, A[6], B[6]);
  xnor xnor_8 (xnor_8_out, A[7], B[7]);
  comp comp_6 (.in_1(A[2]), .in_2(B[2]), .out_3(comp_6_out_3), .out_4(comp_6_out_4));
  comp comp_7 (.in_1(A[1]), .in_2(B[1]), .out_3(comp_7_out_3), .out_4(comp_7_out_4));
  comp comp_8 (.in_1(A[0]), .in_2(B[0]), .out_4(comp_8_out_4));  // open: out_3
  and and_1 (and_1_out, comp_1_out_3, comp_2_out_3, comp_4_out_3, comp_3_out_3, comp_5_out_3, comp_6_out_3, comp_7_out_3, comp_8_out_4);
  and and_2 (and_2_out, comp_1_out_3, comp_2_out_3, comp_4_out_3, comp_3_out_3, comp_5_out_3, comp_6_out_3, comp_7_out_4);
  and and_3 (and_3_out, comp_1_out_3, comp_2_out_3, comp_4_out_3, comp_3_out_3, comp_5_out_3, comp_6_out_4);
  and and_4 (and_4_out, comp_1_out_3, comp_2_out_3, comp_5_out_4);
  and and_5 (and_5_out, comp_2_out_3, comp_4_out_3, comp_3_out_3, comp_3_out_4);
  and and_6 (and_6_out, comp_1_out_3, comp_2_out_3, comp_4_out_4);
  and and_7 (and_7_out, comp_1_out_3, comp_2_out_4);
  and and_8 (Eq, xnor_1_out, xnor_2_out, xnor_3_out, xnor_4_out, xnor_5_out, xnor_6_out, xnor_7_out, xnor_8_out);
  or or_1 (Gt, and_1_out, and_2_out, and_3_out, and_4_out, and_5_out, and_6_out, and_7_out, comp_1_out_4);

  // Notes on the sheet:
  //   A: pull=up
endmodule

module mux (
  input  Input_0,
  input  sel,
  input  Input_1,
  output Output
);

  wire and_1_out, and_2_out, not_1_out;

  not not_1 (not_1_out, sel);
  and and_1 (and_1_out, Input_0, sel);
  and and_2 (and_2_out, not_1_out, Input_1);
  or or_1 (Output, and_1_out, and_2_out);
endmodule

module comp (
  input  in_1,
  input  in_2,
  output out_3,
  output out_4
);

  wire not_1_out;

  xnor xnor_1 (out_3, in_1, in_2);
  not not_1 (not_1_out, in_2);
  and and_1 (out_4, in_1, not_1_out);
endmodule
