// Logisim project NSU-2023-T04L2e02.circ as structural Verilog: 1 circuit, main circuit formula
module formula (
  input  B,
  input  C,
  input  A,
  output R
);

  wire transistor_1_out, transistor_6_out;

  Transistor #(.\type ("n")) transistor_1 (.in(1'b1), .out(transistor_1_out), .gate(B));
  Transistor #(.\type ("n")) transistor_2 (.in(1'b1), .out(transistor_1_out), .gate(C));
  Pull_Resistor pull_resistor_1 (.node(transistor_1_out));
  Transistor transistor_3 (.in(1'b1), .out(R), .gate(transistor_1_out));
  Transistor transistor_4 (.in(1'b1), .out(R), .gate(A));
  Transistor #(.\type ("n")) transistor_5 (.in(transistor_6_out), .out(R), .gate(A));
  Transistor #(.\type ("n")) transistor_6 (.in(1'b0), .out(transistor_6_out), .gate(transistor_1_out));
endmodule
