// Logisim project NSU-2023-T05L2e05.circ as structural Verilog: 4 circuits, main circuit bcd2
module bcd2 (
  input  Cin,
  input  [7:0] A,
  input  [7:0] B,
  output [7:0] R,
  output Cout
);

  wire bcd_add_1_cout;

  Hex_Digit_Display hex_digit_display_1 (.value(A[7:4]));  // open: dp
  Hex_Digit_Display hex_digit_display_2 (.value(B[7:4]));  // open: dp
  Hex_Digit_Display hex_digit_display_3 (.value({3'b000, Cin}));  // open: dp
  Hex_Digit_Display hex_digit_display_4 (.value(A[3:0]));  // open: dp
  Hex_Digit_Display hex_digit_display_5 (.value(B[3:0]));  // open: dp
  bcd_add bcd_add_1 (.Cin(Cin), .A(A[3:0]), .B(B[3:0]), .A_2(R[3:0]), .Cout(bcd_add_1_cout));
  bcd_add bcd_add_2 (.Cin(bcd_add_1_cout), .A(A[7:4]), .B(B[7:4]), .A_2(R[7:4]), .Cout(Cout));
  Hex_Digit_Display hex_digit_display_6 (.value({3'b000, Cout}));  // open: dp
  Hex_Digit_Display hex_digit_display_7 (.value(R[7:4]));  // open: dp
  Hex_Digit_Display hex_digit_display_8 (.value(R[3:0]));  // open: dp
endmodule

// BCD
module bcd_add (
  input  [3:0] A,
  input  [3:0] B,
  input  Cin,
  output [3:0] A_2,
  output Cout
);

  wire and_1_out, or_1_out, or_2_out;
  wire [3:0] mux_1_output, sum_1_r;

  sum sum_1 (.A(A), .B(B), .Cin(Cin), .R(sum_1_r), .Cout(Cout));
  or or_1 (or_1_out, sum_1_r[1], sum_1_r[2]);
  and and_1 (and_1_out, or_1_out, sum_1_r[3]);
  or or_2 (or_2_out, and_1_out, Cout);
  mux mux_1 (.Input_0(4'b0000), .sel(or_2_out), .Input_1(4'b0110), .Output(mux_1_output));
  sum sum_2 (.A(mux_1_output), .B(sum_1_r), .R(A_2));  // open: Cin, Cout
endmodule

module sum (
  input  [3:0] A,
  input  [3:0] B,
  input  Cin,
  output [3:0] R,
  output Cout
);

  wire [3:0] and_1_out, and_2_out, and_3_out;
  wire [3:1] or_1_out;

  Pull_Resistor pull_resistor_1 (.node(Cin));
  assign and_1_out = A & {or_1_out, Cin};  // AND_Gate and_1, 4 bits wide
  assign and_2_out = B & {or_1_out, Cin};  // AND_Gate and_2, 4 bits wide
  assign and_3_out = A & B;  // AND_Gate and_3, 4 bits wide
  assign {Cout, or_1_out} = and_1_out | and_2_out | and_3_out;  // OR_Gate or_1, 4 bits wide
  ExactlyOne xor_1[3:0] (.out(R), .in0(A), .in1({or_1_out, Cin}), .in2(B));
endmodule

module mux (
  input  [3:0] Input_0,
  input  sel,
  input  [3:0] Input_1,
  output [3:0] Output
);

  wire [3:0] and_1_out, and_2_out;
  wire [3:3] not_1_out;

  not not_1 (not_1_out[3], sel);
  assign and_1_out = Input_0 & {4{not_1_out[3]}};  // AND_Gate and_1, 4 bits wide
  assign and_2_out = {4{sel}} & Input_1;  // AND_Gate and_2, 4 bits wide
  assign Output = and_1_out | and_2_out;  // OR_Gate or_1, 4 bits wide
endmodule
