// Logisim project NSU-2023-T05L2e02.circ as structural Verilog: 1 circuit, main circuit dec
module dec (
  input  [7:0] X,
  output [7:0] R,
  output Cout
);

  wire and_1_out, and_2_out, and_3_out, and_4_out, and_5_out, and_6_out, and_7_out;
  wire [7:0] not_1_out, xor_1_out;

  assign not_1_out = ~X;  // NOT_Gate not_1, 8 bits wide
  xor xor_1 (xor_1_out[0], 1'b1, not_1_out[0]);
  and and_1 (and_1_out, 1'b1, not_1_out[0]);
  xor xor_2 (xor_1_out[1], and_1_out, not_1_out[1]);
  and and_2 (and_2_out, and_1_out, not_1_out[1]);
  xor xor_3 (xor_1_out[2], and_2_out, not_1_out[2]);
  and and_3 (and_3_out, and_2_out, not_1_out[2]);
  xor xor_4 (xor_1_out[3], and_3_out, not_1_out[3]);
  and and_4 (and_4_out, and_3_out, not_1_out[3]);
  xor xor_5 (xor_1_out[4], and_4_out, not_1_out[4]);
  and and_5 (and_5_out, and_4_out, not_1_out[4]);
  xor xor_6 (xor_1_out[5], and_5_out, not_1_out[5]);
  and and_6 (and_6_out, and_5_out, not_1_out[5]);
  and and_7 (and_7_out, and_6_out, not_1_out[6]);
  xor xor_7 (xor_1_out[6], and_6_out, not_1_out[6]);
  xor xor_8 (xor_1_out[7], and_7_out, not_1_out[7]);
  and and_8 (Cout, and_7_out, not_1_out[7]);
  assign R = ~xor_1_out;  // NOT_Gate not_2, 8 bits wide
endmodule
