// Logisim project NSU-2023-T04L1e08.circ as structural Verilog: 1 circuit, main circuit mycircuit
module mycircuit (
  input  A,
  input  B,
  input  C,
  output R
);

  wire or_1_out, or_2_out, or_3_out;

  or or_1 (or_1_out, A, B);
  or or_2 (or_2_out, A, C);
  or or_3 (or_3_out, C, B);
  and and_1 (R, or_1_out, or_2_out, or_3_out);
endmodule
