// Logisim project NSU-2023-T04L1e17.circ as structural Verilog: 1 circuit, main circuit mycircuit
module mycircuit (
  input  B,
  input  A,
  input  C,
  output R
);

  wire and_1_out, not_1_out;

  not not_1 (not_1_out, A);
  and and_1 (and_1_out, B, not_1_out);
  or or_1 (R, and_1_out, C);
endmodule
