// Logisim project NSU-2023-T04L1e04.circ as structural Verilog: 1 circuit, main circuit mycircuit
module mycircuit (
  input  A,
  input  B,
  input  C,
  output R
);

  wire or_1_out;

  or or_1 (or_1_out, B, C);
  xor xor_1 (R, A, or_1_out);
endmodule
