// Logisim project NSU-2023-T05L2e03.circ as structural Verilog: 1 circuit, main circuit formula
module formula (
  input  [7:0] A,
  output [7:0] R,
  output OFL
);

  wire [7:0] and_1_out, and_2_out, and_3_out, pull_resistor_1_node;

  // Probe on A
  // Probe on {A[5:0], A[7:6]}
  assign and_1_out = {A[5:0], A[7:6]} & pull_resistor_1_node;  // AND_Gate and_1, 8 bits wide
  assign and_2_out = A & pull_resistor_1_node;  // AND_Gate and_2, 8 bits wide
  assign and_3_out = {A[5:0], A[7:6]} & A;  // AND_Gate and_3, 8 bits wide
  Pull_Resistor pull_resistor_1 (.node(pull_resistor_1_node[0]));
  ExactlyOne xor_1[7:0] (.out(R), .in0({A[5:0], A[7:6]}), .in1(pull_resistor_1_node), .in2(A));
  assign {OFL, pull_resistor_1_node[7:1]} = and_1_out | and_2_out | and_3_out;  // OR_Gate or_1, 8 bits wide
  // Probe on R
endmodule
