// Logisim project NSU-2023-T05L2e04.circ as structural Verilog: 2 circuits, main circuit mult4x4
module mult4x4 (
  input  [3:0] A,
  input  [3:0] B,
  output [7:0] R
);

  wire [3:0] and_1_out;
  wire [4:1] and_5_out;
  wire [5:2] and_9_out;
  wire [6:3] and_13_out;
  wire [7:0] sum_1_r, sum_2_r;

  and and_1 (and_1_out[0], A[0], B[0]);
  and and_2 (and_1_out[1], A[1], B[0]);
  and and_3 (and_1_out[2], A[2], B[0]);
  and and_4 (and_1_out[3], A[3], B[0]);
  and and_5 (and_5_out[1], B[1], A[0]);
  and and_6 (and_5_out[2], B[1], A[1]);
  and and_7 (and_5_out[3], B[1], A[2]);
  and and_8 (and_5_out[4], B[1], A[3]);
  and and_9 (and_9_out[2], B[2], A[0]);
  and and_10 (and_9_out[3], B[2], A[1]);
  and and_11 (and_9_out[4], B[2], A[2]);
  and and_12 (and_9_out[5], B[2], A[3]);
  and and_13 (and_13_out[3], B[3], A[0]);
  and and_14 (and_13_out[4], B[3], A[1]);
  and and_15 (and_13_out[5], B[3], A[2]);
  and and_16 (and_13_out[6], B[3], A[3]);
  sum sum_1 (.A({4'b0000, and_1_out}), .B({3'b000, and_5_out, 1'b0}), .R(sum_1_r));  // open: Cout
  sum sum_2 (.A(sum_1_r), .B({2'b00, and_9_out, 2'b00}), .R(sum_2_r));  // open: Cout
  sum sum_3 (.A(sum_2_r), .B({1'b0, and_13_out, 3'b000}), .R(R));  // open: Cout
endmodule

module sum (
  input  [7:0] A,
  input  [7:0] B,
  input  Cout,
  output [7:0] R
);

  wire [7:0] and_1_out, and_2_out, and_3_out, pull_resistor_1_node;

  Pull_Resistor pull_resistor_1 (.node(pull_resistor_1_node[0]));
  assign and_1_out = A & pull_resistor_1_node;  // AND_Gate and_1, 8 bits wide
  assign and_2_out = B & pull_resistor_1_node;  // AND_Gate and_2, 8 bits wide
  assign and_3_out = A & B;  // AND_Gate and_3, 8 bits wide
  assign {Cout, pull_resistor_1_node[7:1]} = and_1_out | and_2_out | and_3_out;  // OR_Gate or_1, 8 bits wide
  ExactlyOne xor_1[7:0] (.out(R), .in0(A), .in1(pull_resistor_1_node), .in2(B));
endmodule
