// Logisim project NSU-2023-T05L3e01.circ as structural Verilog: 1 circuit, main circuit ALU
module ALU (
  input  Cin,
  input  [7:0] A,
  input  [7:0] B,
  input  [1:0] instr,
  output [7:0] R,
  output Cout,
  output V
);

  wire xnor_1_out, xor_1_out;
  wire [7:0] adder_1_out, and_1_out, or_1_out, subtractor_1_out;

  assign and_1_out = A & B;  // AND_Gate and_1, 8 bits wide
  assign or_1_out = A | B;  // OR_Gate or_1, 8 bits wide
  Adder adder_1 (.a(A), .b(B), .out(adder_1_out), .cin(Cin), .cout(Cout));
  Subtractor subtractor_1 (.a(A), .b(B), .out(subtractor_1_out), .bin(Cin));  // open: bout
  Multiplexer #(.select(2), .width(8)) multiplexer_1 (
    .in0(and_1_out), .in1(or_1_out), .in2(adder_1_out), .in3(subtractor_1_out), .out(R), .sel(instr));  // open: en
  xnor xnor_1 (xnor_1_out, B[7], A[7]);
  xor xor_1 (xor_1_out, A[7], adder_1_out[7]);
  and and_2 (V, xnor_1_out, xor_1_out);

  // Notes on the sheet:
  //   00: and
  //   01: or
  //   10: add
  //   11: sub
endmodule
