// Logisim project NSU-2023-T05L3e02.circ as structural Verilog: 2 circuits, main circuit cmp
module cmp (
  input  [7:0] A,
  input  [7:0] B,
  output Eq,
  output Gt
);

  wire mux_1_output, mux_2_output, mux_3_output, mux_4_output, mux_5_output, mux_6_output, mux_7_output,
       mux_8_output, not_1_out, not_2_out, not_3_out, not_4_out, not_5_out, not_6_out, not_7_out, not_8_out;
  wire [7:0] xnor_1_out;

  assign xnor_1_out = ~(A ^ B);  // XNOR_Gate xnor_1, 8 bits wide
  not not_1 (not_1_out, B[0]);
  not not_2 (not_2_out, B[1]);
  not not_3 (not_3_out, B[2]);
  not not_4 (not_4_out, B[3]);
  not not_5 (not_5_out, B[4]);
  not not_6 (not_6_out, B[5]);
  not not_7 (not_7_out, B[6]);
  not not_8 (not_8_out, B[7]);
  and and_1 (Eq, xnor_1_out[0], xnor_1_out[1], xnor_1_out[2], xnor_1_out[3], xnor_1_out[4], xnor_1_out[5], xnor_1_out[6], xnor_1_out[7]);
  mux mux_1 (.Input_0(1'b0), .sel(xnor_1_out[0]), .Input_1(not_1_out), .Output(mux_1_output));
  mux mux_2 (.Input_0(1'b0), .sel(xnor_1_out[1]), .Input_1(not_2_out), .Output(mux_2_output));
  mux mux_3 (.Input_0(1'b0), .sel(xnor_1_out[2]), .Input_1(not_3_out), .Output(mux_3_output));
  mux mux_4 (.Input_0(1'b0), .sel(xnor_1_out[3]), .Input_1(not_4_out), .Output(mux_4_output));
  mux mux_5 (.Input_0(1'b0), .sel(xnor_1_out[4]), .Input_1(not_5_out), .Output(mux_5_output));
  mux mux_6 (.Input_0(1'b0), .sel(xnor_1_out[5]), .Input_1(not_6_out), .Output(mux_6_output));
  mux mux_7 (.Input_0(1'b0), .sel(xnor_1_out[6]), .Input_1(not_7_out), .Output(mux_7_output));
  mux mux_8 (.Input_0(1'b0), .sel(xnor_1_out[7]), .Input_1(not_8_out), .Output(mux_8_output));
  ExactlyOne xor_1 (
    .out(Gt), .in0(mux_1_output), .in1(mux_2_output), .in2(mux_3_output), .in3(mux_4_output),
    .in4(mux_5_output), .in5(mux_6_output), .in6(mux_7_output), .in7(mux_8_output));

  // Notes on the sheet:
  //   A: pull=up
endmodule

module mux (
  input  Input_0,
  input  sel,
  input  Input_1,
  output Output
);

  wire and_1_out, and_2_out, not_1_out;

  not not_1 (not_1_out, sel);
  and and_1 (and_1_out, Input_0, sel);
  and and_2 (and_2_out, not_1_out, Input_1);
  or or_1 (Output, and_1_out, and_2_out);
endmodule
