// Logisim project NSU-2023-T06L1e01.circ as structural Verilog: 1 circuit, main circuit fib32
module fib32 (
  input  clock,
  output [31:0] a,
  output stop,
  output [5:0] k
);

  wire clckon, comparator_2_eq, comparator_2_lt, k__1;
  wire [5:0] adder_1_out;
  wire [31:0] multiplexer_1_out, multiplexer_2_out, register_1_q, register_2_q;

  Multiplexer #(.width(32)) multiplexer_1 (.in0(a), .in1(32'h1), .out(multiplexer_1_out), .sel(k__1));  // open: en
  Multiplexer #(.width(32)) multiplexer_2 (
    .in0(register_1_q), .in1(32'h1), .out(multiplexer_2_out), .sel(k__1));  // open: en
  Comparator #(.width(6), .mode("unsigned")) comparator_1 (.a(k), .b(6'b000001), .eq(k__1));  // open: gt, lt
  Register #(.width(32)) register_1 (
    .D(multiplexer_1_out), .Q(register_1_q), .clk(clckon), .clr(comparator_2_eq));  // open: en
  Adder #(.width(6)) adder_1 (.a(6'b000001), .b(k), .out(adder_1_out));  // open: cin, cout
  Register #(.width(32)) register_2 (
    .D(multiplexer_2_out), .Q(register_2_q), .clk(clckon), .clr(comparator_2_eq));  // open: en
  Adder #(.width(32)) adder_2 (.a(register_1_q), .b(register_2_q), .out(a));  // open: cin, cout
  and and_1 (clckon, clock, comparator_2_lt);
  Comparator #(.width(32), .mode("unsigned")) comparator_2 (
    .a(a), .b({32{1'b1}}), .eq(comparator_2_eq), .lt(comparator_2_lt));  // open: gt
  not not_1 (stop, comparator_2_lt);

  // Other names for the same wires on the sheet: clck = clock; curNum[31:0] = a
endmodule
